# Fritzing sketch master (saved by Fritzing 0.9.5d)

parts:
  GY1 = MPU-6050 Board GY-521 [form="♀ (female)" package=THT]
  BAT1 = 18650 battery holder [package=battery-18650-kit]
  BAT2 = 18650 battery holder [package=battery-18650-kit]
  BAT3 = 18650 battery holder [package=battery-18650-kit]
  BAT4 = 18650 battery holder [package=battery-18650-kit]
  U1 = WS2812 RGB LED strip
  U2 = WS2812 RGB LED strip
  U3 = WS2812 RGB LED strip
  S1 = Toggle Switch [package=THT]
  S2 = Toggle Switch [package=THT]
  S3 = Toggle Switch [package=THT]
  LLC1 = Logic Level Converter [package="Breakout board"]
  U4 = Mini-360 DC-DC Buck converter [package=THT]
  R1 = Resistor [tolerance=±5% resistance=220 package=THT]
  R2 = Resistor [tolerance=±5% resistance=220 package=THT]
  R3 = Resistor [tolerance=±5% resistance=220 package=THT]
  R4 = Resistor [tolerance=±5% resistance=10k package=THT]
  R5 = Resistor [tolerance=±5% resistance=10k package=THT]
  R6 = Resistor [tolerance=±5% resistance=10k package=THT]
  U5 = ESP32-38PinWide [part_number=ESP32-38PinWide]
  S4 = Taiway 100-SP-X-T1 SPDT Miniature Toggle Switch [part_number=100-SP-X-T1-0-0-B1-M2 package=THT]

nets:
  N1: GY1.pin1, S1.COM, S2.COM, S3.COM, LLC1.LV, U5.3.3
  GND: GY1.pin2, U1.GND, U2.GND, U3.GND, LLC1.L-GND, LLC1.H-GND, U4.OUT-, R4.Pin_0, R5.Pin_0, R6.Pin_0, U5.GND
  N2: GY1.pin3, U5.GPIO22
  N3: GY1.pin4, U5.GPIO21
  N4: BAT1.+, BAT2.-
  N5: BAT1.-, BAT4.+
  N6: BAT2.+, BAT3.-
  N7: BAT3.+, U4.IN-
  N8: BAT4.-, S4.L1
  VCC: U1.VCC, U2.VCC, U3.VCC, LLC1.HV, U4.OUT+, U5.VIN
  N9: U1.DIN, LLC1.HV1
  N10: U2.DIN, LLC1.HV2
  N11: U3.DIN, LLC1.HV3
  N12: S1.L2, R4.Pin_1, U5.GPIO34
  N13: S2.L2, R5.Pin_1, U5.GPIO35
  N14: S3.L2, R6.Pin_1, U5.GPIO33
  N15: LLC1.LV1, R1.Pin_1
  N16: LLC1.LV2, R2.Pin_1
  N17: LLC1.LV3, R3.Pin_1
  N18: U4.IN+, S4.L2
  N19: R1.Pin_0, U5.GPIO25
  N20: R2.Pin_0, U5.GPIO27
  N21: R3.Pin_0, U5.GPIO26

custom parts:
  MPU-6050 Board GY-521: Acelerometro y Giroscopio MPU-6050 Board GY-521
  18650 battery holder: 18650 Battery
  WS2812 RGB LED strip: WS2812 strip
  Logic Level Converter: 5V to/from 3.3V logic level converter
  Mini-360 DC-DC Buck converter: Mini-360 DC-DC Buck converter. Tiny buck step down voltage converter, input voltage 4.75 to 23V output 1 to 17V adjustable. Available from ebay and the like.
  ESP32-38PinWide: Generic 38-Pin ESP32 with wide format (only access to one side of pins on a breadboard) based on Stephen Lilley's HiLetgo ESP-WROOM-32 ESP32 ESP-32S Development Board.
