# Fritzing sketch slave (saved by Fritzing 0.9.5d)

parts:
  A1 = Wemos S2 Mini [part_number="WeMos D1 Mini Lite"]
  LLC1 = Logic Level Converter [package="Breakout board"]
  U1 = WS2812 RGB LED strip
  U2 = WS2812 RGB LED strip
  U3 = WS2812 RGB LED strip
  R1 = Resistor [tolerance=±5% resistance=220 package=THT]
  R2 = Resistor [tolerance=±5% resistance=220 package=THT]
  R3 = Resistor [tolerance=±5% resistance=220 package=THT]
  U4 = Mini-360 DC-DC Buck converter [package=THT]
  X1 = USB Connectors [package=usb-a-s-nosilk-female]
  R4 = Resistor [tolerance=±5% resistance=220 package=THT]
  U5 = WS2812 RGB LED strip

nets:
  N1: A1.Pin_8, LLC1.LV, U4.OUT+
  VCC: A1.Pin_17, LLC1.HV, U1.VCC, U2.VCC, U3.VCC, U4.IN+, X1.VBUS, U5.VCC
  N2: A1.Pin_18, A1.Pin_26, LLC1.L-GND, U4.OUT-
  N3: A1.Pin_19, R1.Pin_1
  N4: A1.Pin_20, R3.Pin_1
  N5: A1.Pin_27, R2.Pin_1
  N6: A1.Pin_28, R4.Pin_1
  N7: LLC1.LV1, R1.Pin_0
  N8: LLC1.LV2, R2.Pin_0
  N9: LLC1.LV3, R3.Pin_0
  N10: LLC1.LV4, R4.Pin_0
  N11: LLC1.HV4, U5.DIN
  N12: LLC1.HV3, U2.DIN
  GND: LLC1.H-GND, U1.GND, U2.GND, U3.GND, U5.GND
  N13: LLC1.HV2, U3.DIN
  N14: LLC1.HV1, U1.DIN
  N15: U4.IN-, X1.GND

custom parts:
  Wemos S2 Mini: A mini wifi board based on the ESP32-S2FN4R2.
  Logic Level Converter: 5V to/from 3.3V logic level converter
  WS2812 RGB LED strip: WS2812 strip
  Mini-360 DC-DC Buck converter: Mini-360 DC-DC Buck converter. Tiny buck step down voltage converter, input voltage 4.75 to 23V output 1 to 17V adjustable. Available from ebay and the like.
